# Fritzing sketch Reaktionstest (saved by Fritzing 0.9.2b)
breadboards: 1

parts:
  Bauteil1 = Arduino Nano (Rev3.0)
  S1 = Pushbutton [package="[THT]"]
  LED1 = LED - 5mm [color="Red (633nm)" package="5 mm [THT]"]
  R1 = Resistor [tolerance=±5% resistance=220 package=THT]

nets:
  N1: Bauteil1.GND, S1.Pin_1, S1.Pin_2
  N2: Bauteil1.D3, S1.Pin_3, S1.Pin_4
  N3: Bauteil1.D12/MISO, LED1.cathode
  N4: Bauteil1.5V, R1.Pin_0
  N5: LED1.anode, R1.Pin_1
